// Logisim project processor.circ as structural Verilog: 6 circuits, main circuit main
module main (
  input  in_1,
  output [31:0] Instruction,
  output [23:0] Address,
  output [31:0] R1out,
  output [11:0] I_imm,
  output [31:0] immediate,
  output [31:0] R2out,
  output [23:0] add_to_mem,
  output [31:0] data_to_mem,
  output [11:0] st_imm,
  output branch_mux,
  output [11:0] Br_imm,
  output [1:0] imm_mux,
  output [4:0] R1,
  output [4:0] RD,
  output [4:0] R2,
  output [3:0] Alucontrolbits,
  output [31:0] ALUres,
  output [31:0] Outmuxram
);

  wire alu_1_zero, and_2_out, clock_1_out, mainctl_1_alusrc, mainctl_1_branch, mainctl_1_memread,
       mainctl_1_memtoreg, mainctl_1_memwrite, mainctl_1_regwrite, not_1_out;
  wire [1:0] mainctl_1_aluop;
  wire [7:0] undriven, undriven_2, undriven_3, undriven_4;
  wire [11:0] multiplexer_1_out;
  wire [31:0] adder_1_out, adder_2_out, bit_extender_2_out, multiplexer_3_out, PC_q, rom_1_p1, shifter_1_out;

  Register #(.width(32)) PC (.D(rom_1_p1), .en(1'b1), .clk(clock_1_out), .Q(PC_q), .clr(in_1));
  Bit_Extender #(.in_width(32), .out_width(24), .\type ("zero")) bit_extender_1 (.in(PC_q), .out(Address));
  // ROM #(.addrWidth(24), .line("quad")) rom_1: pin names not known; wires that end beside it: rom_1_p1, Address
  Adder #(.width(32)) adder_1 (.a(PC_q), .b(32'h4), .out(adder_1_out));  // open: cin, cout
  Clock clock_1 (.out(clock_1_out));
  immctl immctl_1 (.I6(Instruction[6]), .I5(Instruction[5]), .I4(Instruction[4]), .Sel1(imm_mux[0]), .Sel2(imm_mux[1]));
  not not_1 (not_1_out, imm_mux[0]);
  and and_1 (branch_mux, not_1_out, imm_mux[1]);
  mainCTL mainctl_1 (
    .Opcode(Instruction[6:0]), .ALUSrc(mainctl_1_alusrc), .MemToReg(mainctl_1_memtoreg),
    .RegWrite(mainctl_1_regwrite), .MemRead(mainctl_1_memread), .MemWrite(mainctl_1_memwrite),
    .Branch(mainctl_1_branch), .ALUOp(mainctl_1_aluop));
  Multiplexer #(.select(2), .width(12)) multiplexer_1 (
    .in0({Br_imm[11], Br_imm[9:4], I_imm[4:0]}), .in1({Br_imm[11], Br_imm[9:0], Br_imm[10]}), .in2(Br_imm),
    .out(multiplexer_1_out), .sel(imm_mux));  // open: in3
  assign bit_extender_2_out = {{20{multiplexer_1_out[11]}}, multiplexer_1_out};  // Bit_Extender bit_extender_2
  Shifter #(.width(32)) shifter_1 (.in(bit_extender_2_out), .\dist (5'b00001), .out(shifter_1_out));
  regis regis_1 (
    .RD({Br_imm[3:0], Br_imm[10]}), .RS2(I_imm[4:0]), .RS1(Instruction[19:15]), .RegWEn(mainctl_1_regwrite),
    .CLK(clock_1_out), .DATA(Outmuxram), .OPT1(R1out), .OPT2(data_to_mem));
  Multiplexer #(.width(32)) multiplexer_2 (
    .in0(bit_extender_2_out), .in1(shifter_1_out), .out(immediate), .sel(branch_mux));
  Adder #(.width(32)) adder_2 (.a(PC_q), .b(immediate), .out(adder_2_out));  // open: cin, cout
  Multiplexer #(.width(32)) multiplexer_3 (
    .in0(data_to_mem), .in1(immediate), .out(multiplexer_3_out), .sel(mainctl_1_alusrc));
  Multiplexer #(.width(32)) multiplexer_4 (.in0(adder_1_out), .in1(adder_2_out), .out(rom_1_p1), .sel(and_2_out));
  and and_2 (and_2_out, mainctl_1_branch, alu_1_zero);
  ALUCTLNEW aluctlnew_1 (.ALUOp(mainctl_1_aluop), .Fun3(Instruction[14:12]), .I30(Br_imm[9]), .Alusel(Alucontrolbits));
  ALU alu_1 (
    .A(R1out), .B(multiplexer_3_out), .ALUSel(Alucontrolbits), .Zero(alu_1_zero), .Result(ALUres));  // open: OverFlow
  Bit_Extender #(.in_width(32), .out_width(24), .\type ("zero")) bit_extender_3 (.in(ALUres), .out(add_to_mem));
  // RAM #(.addrWidth(24), .enables("line"), .line("quad")) ram_1: pin names not known; wires that end beside it: mainctl_1_memread, add_to_mem, mainctl_1_memwrite, clock_1_out, data_to_mem[7:0], data_to_mem[15:8], data_to_mem[23:16], data_to_mem[31:24]
  Clock clock_2 (.out(clock_1_out));
  Multiplexer #(.width(32)) multiplexer_5 (
    .in0(ALUres), .in1({undriven_4, undriven_3, undriven_2, undriven}), .out(Outmuxram),
    .sel(mainctl_1_memtoreg));

  assign I_imm[11:5] = {Br_imm[11], Br_imm[9:4]};
  assign {Instruction[31:20], Instruction[11:7]} = {Br_imm[11], Br_imm[9:4], I_imm[4:0], Br_imm[3:0], Br_imm[10]};
  assign R1 = Instruction[19:15];
  assign R2 = I_imm[4:0];
  assign R2out = data_to_mem;
  assign RD = {Br_imm[3:0], Br_imm[10]};
  assign st_imm = {Br_imm[11], Br_imm[9:0], Br_imm[10]};

  // Notes on the sheet:
  //                                ANUDEEP(2022CS11617)
  //   contents of rom_1 (hex, n*v repeats v):
  //   93 0 0 3 23 20 10 0 13 1 e0 fd 23 22 20 0 b3 82 20 0 23 24 50 0 33 83 22 40 23 26 60 0 b3 13 13 0 23
  //   28 70 0 33 a4 63 0 23 2a 80 0 93 4 40 2 33 c5 84 0 23 2e a0 0 b3 52 95 0 23 20 50 2 b3 e0 a2 0 23 22
  //   10 2 33 f1 a0 0 23 24 20 2 93 2 d1 0 23 26 50 2 13 a3 22 1 23 28 60 2 93 33 93 0 23 2a 70 2 13 c4 e3
  //   1 23 2c 80 2 93 64 c4 1 23 2e 90 2 13 f5 c4 1 23 20 a0 4 93 12 35 0 23 22 50 4 93 d0 2
  //                  REVANTH(2022CS51650)
endmodule

module regis (
  input  [4:0] RD,
  input  [4:0] RS2,
  input  [4:0] RS1,
  input  RegWEn,
  input  CLK,
  input  [31:0] DATA,
  output [31:0] OPT1,
  output [31:0] OPT2
);

  wire and_1_out, and_2_out, and_3_out, and_4_out, and_5_out, and_6_out, and_7_out, and_8_out, and_9_out,
       decoder_1_out0, decoder_1_out1, decoder_1_out2, decoder_1_out5, decoder_1_out6, decoder_1_out7,
       decoder_1_out8, decoder_1_out9, decoder_1_out10;
  wire [31:0] a0_q, ra_q, s0_q, s1_q, sp_q, t0_q, t1_q, t2_q, zero_q;

  Decoder #(.select(5)) decoder_1 (
    .out0(decoder_1_out0), .out1(decoder_1_out1), .out2(decoder_1_out2), .out5(decoder_1_out5),
    .out6(decoder_1_out6), .out7(decoder_1_out7), .out8(decoder_1_out8), .out9(decoder_1_out9),
    .out10(decoder_1_out10), .sel(RD));  // open: out3, out4, out11, out12, out13, out14, out15, out16, out17, out18, out19, out20, out21, out22, out23, out24, out25, out26, out27, out28, out29, out30, out31, en
  and and_1 (and_1_out, decoder_1_out0, 1'b0);
  and and_2 (and_2_out, decoder_1_out1, RegWEn);
  and and_3 (and_3_out, decoder_1_out2, RegWEn);
  and and_4 (and_4_out, decoder_1_out5, RegWEn);
  and and_5 (and_5_out, decoder_1_out6, RegWEn);
  and and_6 (and_6_out, decoder_1_out7, RegWEn);
  and and_7 (and_7_out, decoder_1_out8, RegWEn);
  and and_8 (and_8_out, decoder_1_out9, RegWEn);
  and and_9 (and_9_out, decoder_1_out10, RegWEn);
  Register #(.width(32)) zero (.D(DATA), .en(and_1_out), .clk(CLK), .Q(zero_q));  // open: clr
  Register #(.width(32)) ra (.D(DATA), .en(and_2_out), .clk(CLK), .Q(ra_q));  // open: clr
  Register #(.width(32)) sp (.D(DATA), .en(and_3_out), .clk(CLK), .Q(sp_q));  // open: clr
  Register #(.width(32)) t0 (.D(DATA), .en(and_4_out), .clk(CLK), .Q(t0_q));  // open: clr
  Register #(.width(32)) t1 (.D(DATA), .en(and_5_out), .clk(CLK), .Q(t1_q));  // open: clr
  Register #(.width(32)) t2 (.D(DATA), .en(and_6_out), .clk(CLK), .Q(t2_q));  // open: clr
  Register #(.width(32)) s0 (.D(DATA), .en(and_7_out), .clk(CLK), .Q(s0_q));  // open: clr
  Register #(.width(32)) s1 (.D(DATA), .en(and_8_out), .clk(CLK), .Q(s1_q));  // open: clr
  Register #(.width(32)) a0 (.D(DATA), .en(and_9_out), .clk(CLK), .Q(a0_q));  // open: clr
  Multiplexer #(.select(5), .width(32)) multiplexer_1 (
    .in0(zero_q), .in1(ra_q), .in2(sp_q), .in5(t0_q), .in6(t1_q), .in7(t2_q), .in8(s0_q), .in9(s1_q),
    .in10(a0_q), .out(OPT1), .sel(RS1));  // open: in3, in4, in11, in12, in13, in14, in15, in16, in17, in18, in19, in20, in21, in22, in23, in24, in25, in26, in27, in28, in29, in30, in31
  Multiplexer #(.select(5), .width(32)) multiplexer_2 (
    .in0(zero_q), .in1(ra_q), .in2(sp_q), .in5(t0_q), .in6(t1_q), .in7(t2_q), .in8(s0_q), .in9(s1_q),
    .in10(a0_q), .out(OPT2), .sel(RS2));  // open: in3, in4, in11, in12, in13, in14, in15, in16, in17, in18, in19, in20, in21, in22, in23, in24, in25, in26, in27, in28, in29, in30, in31
endmodule

module ALU (
  input  [31:0] A,
  input  [31:0] B,
  input  [3:0] ALUSel,
  output Zero,
  output [31:0] Result,
  output OverFlow
);

  wire adder_1_cout, comparator_1_gt, comparator_2_gt, nor_1_out;
  wire [4:0] bitselector_1_out, bitselector_2_out, bitselector_3_out;
  wire [15:0] or_2_out;
  wire [31:0] adder_1_out, and_1_out, bit_extender_1_out, bit_extender_2_out, multiplier_1_cout,
       multiplier_2_cout, multiplier_2_out, multiplier_3_out, or_1_out, shifter_1_out, shifter_2_out,
       shifter_3_out, subtractor_1_out, xor_1_out;

  Comparator #(.mode("unsigned"), .width(32)) comparator_1 (.a(A), .b(B), .gt(comparator_1_gt));  // open: eq, lt
  assign bit_extender_1_out = {{31{comparator_1_gt}}, comparator_1_gt};  // Bit_Extender bit_extender_1
  assign bit_extender_2_out = {{31{1'b0}}, comparator_2_gt};  // Bit_Extender bit_extender_2
  Comparator #(.width(32)) comparator_2 (.a(B), .b(A), .gt(comparator_2_gt));  // open: eq, lt
  BitSelector #(.group(5), .width(32)) bitselector_1 (.in(B), .out(bitselector_1_out), .sel(3'b000));
  BitSelector #(.group(5), .width(32)) bitselector_2 (.in(B), .out(bitselector_2_out), .sel(3'b000));
  Multiplier #(.mode("twosComplement"), .width(32)) multiplier_1 (
    .a(A), .b(B), .cout(multiplier_1_cout));  // open: out, cin
  Multiplier #(.width(32)) multiplier_2 (.a(A), .b(B), .out(multiplier_2_out), .cout(multiplier_2_cout));  // open: cin
  BitSelector #(.group(5), .width(32)) bitselector_3 (.in(B), .out(bitselector_3_out), .sel(3'b000));
  Adder #(.width(32)) adder_1 (.a(A), .b(B), .out(adder_1_out), .cout(adder_1_cout));  // open: cin
  Shifter #(.width(32)) shifter_1 (.in(A), .\dist (bitselector_1_out), .out(shifter_1_out));
  assign xor_1_out = B ^ A;  // XOR_Gate xor_1, 32 bits wide
  Shifter #(.shift("lr"), .width(32)) shifter_2 (.in(A), .\dist (bitselector_2_out), .out(shifter_2_out));
  assign or_1_out = A | B;  // OR_Gate or_1, 32 bits wide
  assign and_1_out = A & B;  // AND_Gate and_1, 32 bits wide
  Multiplier #(.mode("twosComplement"), .width(32)) multiplier_3 (
    .a(A), .b(B), .out(multiplier_3_out));  // open: cin, cout
  Subtractor #(.width(32)) subtractor_1 (.a(A), .b(B), .out(subtractor_1_out));  // open: bin, bout
  Shifter #(.shift("ar"), .width(32)) shifter_3 (.in(A), .\dist (bitselector_3_out), .out(shifter_3_out));
  Multiplexer #(.enable("true"), .select(4), .width(32)) multiplexer_1 (
    .in0(adder_1_out), .in1(shifter_1_out), .in2(bit_extender_2_out), .in3(bit_extender_1_out),
    .in4(xor_1_out), .in5(shifter_2_out), .in6(or_1_out), .in7(and_1_out), .in8(multiplier_3_out),
    .in9(multiplier_1_cout), .in11(multiplier_2_cout), .in12(subtractor_1_out), .in13(shifter_3_out),
    .in15(B), .out(Result), .sel(ALUSel));  // open: in10, in14, en
  assign or_2_out = Result[15:0] | Result[31:16];  // OR_Gate or_2, 16 bits wide
  nor nor_1 (nor_1_out, ALUSel[0], ALUSel[1], ALUSel[2], ALUSel[3]);
  Comparator #(.width(16)) comparator_3 (.a({16{1'b0}}), .b(or_2_out), .eq(Zero));  // open: gt, lt
  and and_2 (OverFlow, nor_1_out, adder_1_cout);
endmodule

module immctl (
  input  I6,
  input  I5,
  input  I4,
  output Sel1,
  output Sel2
);

  wire and_1_out, not_1_out, not_2_out;

  not not_1 (not_1_out, I6);
  not not_2 (not_2_out, I4);
  and and_1 (and_1_out, not_1_out, I5);
  and and_2 (Sel1, and_1_out, not_2_out);

  assign Sel2 = I6;
endmodule

module ALUCTLNEW (
  input  [1:0] ALUOp,
  input  [2:0] Fun3,
  input  I30,
  output [3:0] Alusel
);

  wire and_1_out, and_2_out, and_3_out, and_4_out, and_5_out, not_1_out, not_2_out, not_3_out, not_4_out,
       not_5_out;

  not not_1 (not_1_out, ALUOp[1]);
  not not_2 (not_2_out, ALUOp[0]);
  not not_3 (not_3_out, Fun3[2]);
  not not_4 (not_4_out, Fun3[1]);
  not not_5 (not_5_out, Fun3[0]);
  and and_1 (and_1_out, ALUOp[1], not_2_out, not_3_out, not_4_out, not_5_out, I30);
  or or_1 (Alusel[3], and_1_out, and_2_out);
  and and_2 (and_2_out, not_1_out, ALUOp[0]);
  and and_3 (and_3_out, not_1_out, ALUOp[0]);
  and and_4 (and_4_out, ALUOp[1], not_2_out, not_4_out, not_5_out, I30);
  or or_2 (Alusel[2], and_3_out, and_4_out, and_5_out);
  and and_5 (and_5_out, ALUOp[1], Fun3[2]);
  and and_6 (Alusel[1], ALUOp[1], Fun3[1]);
  and and_7 (Alusel[0], ALUOp[1], Fun3[0]);
endmodule

module mainCTL (
  input  [6:0] Opcode,
  output ALUSrc,
  output MemToReg,
  output RegWrite,
  output MemRead,
  output MemWrite,
  output Branch,
  output [1:0] ALUOp
);

  wire and_1_out, and_2_out, and_4_out, and_5_out, and_10_out, and_11_out, not_1_out, not_2_out, not_3_out,
       not_4_out, not_5_out;

  not not_1 (not_1_out, Opcode[6]);
  not not_2 (not_2_out, Opcode[5]);
  not not_3 (not_3_out, Opcode[4]);
  not not_4 (not_4_out, Opcode[3]);
  not not_5 (not_5_out, Opcode[2]);
  and and_1 (and_1_out, not_1_out, not_2_out, not_4_out, not_5_out, Opcode[1], Opcode[0]);
  and and_2 (and_2_out, not_1_out, not_3_out, not_4_out, not_5_out, Opcode[1], Opcode[0]);
  and and_3 (MemToReg, not_1_out, not_2_out, not_3_out, not_4_out, not_5_out, Opcode[1], Opcode[0]);
  and and_4 (and_4_out, not_1_out, not_2_out, not_4_out, not_5_out, Opcode[1], Opcode[0]);
  and and_5 (and_5_out, not_1_out, Opcode[4], not_4_out, not_5_out, Opcode[1], Opcode[0]);
  and and_6 (MemRead, not_1_out, not_2_out, not_3_out, not_4_out, not_5_out, Opcode[1], Opcode[0]);
  and and_7 (MemWrite, not_1_out, Opcode[5], not_3_out, not_4_out, not_5_out, Opcode[1], Opcode[0]);
  and and_8 (Branch, Opcode[6], Opcode[5], not_3_out, not_4_out, not_5_out, Opcode[1], Opcode[0]);
  and and_9 (ALUOp[1], not_1_out, Opcode[4], not_4_out, not_5_out, Opcode[1], Opcode[0]);
  and and_10 (and_10_out, not_1_out, not_2_out, Opcode[4], not_4_out, not_5_out, Opcode[1], Opcode[0]);
  and and_11 (and_11_out, Opcode[6], Opcode[5], not_3_out, not_4_out, not_5_out, Opcode[1], Opcode[0]);
  or or_1 (ALUSrc, and_1_out, and_2_out);
  or or_2 (RegWrite, and_4_out, and_5_out);
  or or_3 (ALUOp[0], and_10_out, and_11_out);
endmodule
